# Fritzing sketch timer_with_button_and_pwm_buzzer (saved by Fritzing 0.9.2b)
breadboards: 1

parts:
  7SEG1 = 7-Segment LED I2C Backpack (red)
  元件1 = Arduino Pro Mini v13
  R1 = Resistor [tolerance=±5% resistance=210 package=THT]
  S1 = Pushbutton [package="[THT]"]
  R2 = Rotary Potentiometer (Small) [maximum_resistance=100kΩ package=THT]
  Power_plug1 = Power plug
  J1 = Piezo Speaker

nets:
  VCC: 7SEG1.V+, 元件1.VCC, S1.Pin_3, S1.Pin_4, R2.leg2, Power_plug1.VCC
  GND: 7SEG1.GND, 元件1.GND, R1.Pin_1, R2.leg1, Power_plug1.GND, J1.pin1
  N1: 7SEG1.SDA, 元件1.A4
  N2: 7SEG1.SCL, 元件1.A5
  N3: 元件1.A0, R2.wiper
  N4: 元件1.D7, J1.pin2
  N5: 元件1.D2, R1.Pin_0, S1.Pin_1, S1.Pin_2

custom parts:
  7-Segment LED I2C Backpack (red): 4-digit, 7-segment LED Display with I2C Control
